# Fritzing sketch circuit (saved by Fritzing 0.9.9b)
breadboards: 1

parts:
  Mod1 = Raspberry Pi Pico W
  S1 = Pushbutton [package="[THT]"]
  Parça1 = InvenSense MPU6050

nets:
  N1: Mod1.pin_3, Mod1.pin_8, Mod1.pin_13, Mod1.pin_18, Mod1.pin_23, Mod1.pin_28, Mod1.pin_33, Mod1.pin_38, S1.Pin_3, S1.Pin_4, Parça1.GND
  N2: Mod1.pin_6, Parça1.SDA
  N3: Mod1.pin_7, Parça1.SCL
  N4: Mod1.pin_30, S1.Pin_1, S1.Pin_2
  N5: Mod1.pin_36, Parça1.VCC

custom parts:
  Raspberry Pi Pico W: Raspberry Pi Pico W. Based around the RP2040 microcontroller the Pico W is a low cost microcontroller device bringing Raspberry Pi quality, cost, and easy of use to the microcontroller space. The areas marked KEEPOUT in pcb silkscreen should not have traces running through them to avoid shorts on a soldered in module!
